// Logisim project cpu.circ as structural Verilog: 1 circuit, main circuit main
module main (
  input  CLK_RUN,
  input  CLK_HLT,
  input  [7:0] in_3,
  input  [15:0] in_4,
  input  in_5,
  input  in_6,
  input  IP_HI_TO_DATA,
  input  IP_LO_TO_DATA,
  input  A_TO_DATA,
  input  DATA_TO_A,
  input  DATA_TO_IP_HI,
  input  DATA_TO_IP_LO,
  input  IP_TO_ADDR,
  input  A_TO_X,
  input  IP_INC,
  input  Z_TO_DATA,
  input  ADDR_TO_IP,
  input  SUB,
  input  DATA_TO_MAR_HI,
  input  DATA_TO_MAR_LO,
  input  MAR_INC,
  input  FLAGS,
  input  ADDR_TO_MAR,
  input  DATA_TO_Y,
  input  MDR_TO_DATA,
  input  DATA_TO_MDR,
  input  H_TO_DATA,
  input  L_TO_DATA,
  input  B_TO_DATA,
  input  DATA_TO_B,
  input  DATA_TO_H,
  input  DATA_TO_L,
  input  HL_TO_ADDR,
  input  C_TO_DATA,
  input  DATA_TO_C,
  input  ADDR_TO_HL,
  input  TH_TO_DATA,
  input  TL_TO_DATA,
  input  D_TO_DATA,
  input  DATA_TO_D,
  input  DATA_TO_TH,
  input  DATA_TO_TL,
  input  T_TO_ADDR,
  input  in_44,
  output [7:0] out_45,
  output [15:0] out_46,
  output [15:0] out_47,
  output [7:0] out_48,
  output [7:0] out_49,
  output [15:0] out_50,
  output [7:0] out_51,
  output [7:0] out_52,
  output [7:0] out_53,
  output [7:0] out_54,
  output [7:0] out_55,
  output [15:0] out_56,
  output [7:0] out_57,
  output [7:0] out_58,
  output [7:0] out_59,
  output [7:0] out_60,
  output [15:0] out_61,
  output [7:0] out_62
);

  wire and_1_out, and_2_out, CF, CLK, CLK_STEP_out, clock_1_out, minus_CLK, nor_2_out, nor_3_out, nor_4_out,
       nor_5_out, nor_6_out, nor_7_out, not_1_out, not_2_out, not_3_out, not_4_out, not_5_out, or_1_out,
       or_2_out, or_3_out, or_4_out, or_5_out, RST, ZF;
  wire [1:0] adder_1_cout;
  wire [7:0] bit_extender_1_out, controlled_buffer_8_out, controlled_buffer_9_out, controlled_buffer_13_out,
       controlled_buffer_15_out, controlled_buffer_18_out, controlled_buffer_20_out,
       controlled_buffer_23_out, controlled_buffer_26_out, xor_1_out;
  wire [7:2] register_1_q;

  nor nor_1 (adder_1_cout[1], out_51[0], out_51[1], out_51[2], out_51[3], out_51[4], out_51[5], out_51[6], out_51[7]);
  Register register_1 (.D({{6{1'b0}}, adder_1_cout}), .en(FLAGS), .Q({register_1_q, ZF, CF}), .clk(CLK), .clr(RST));
  Register register_2 (.D(out_45), .en(DATA_TO_A), .Q(out_48), .clk(CLK));  // open: clr
  Register register_3 (.D(out_48), .en(A_TO_X), .Q(out_49), .clk(CLK));  // open: clr
  assign bit_extender_1_out = {{7{SUB}}, SUB};  // Bit_Extender bit_extender_1
  Register register_4 (.D(out_45), .en(DATA_TO_Y), .Q(out_53), .clk(CLK));  // open: clr
  Register register_5 (.D(out_45), .en(DATA_TO_B), .Q(out_57), .clk(CLK));  // open: clr
  Register register_6 (.D(out_45), .en(DATA_TO_C), .Q(out_58), .clk(CLK));  // open: clr
  Register register_7 (.D(out_45), .en(DATA_TO_D), .Q(out_62), .clk(CLK));  // open: clr
  assign out_45 = A_TO_DATA ? out_48 : 8'bz;  // Controlled_Buffer controlled_buffer_1
  Adder adder_1 (.a(out_49), .b(xor_1_out), .out(out_51), .cin(SUB), .cout(adder_1_cout[0]));
  assign xor_1_out = bit_extender_1_out ^ out_53;  // XOR_Gate xor_1, 8 bits wide
  assign out_45 = B_TO_DATA ? out_57 : 8'bz;  // Controlled_Buffer controlled_buffer_2
  assign out_45 = C_TO_DATA ? out_58 : 8'bz;  // Controlled_Buffer controlled_buffer_3
  assign out_45 = D_TO_DATA ? out_62 : 8'bz;  // Controlled_Buffer controlled_buffer_4
  Clock clock_1 (.out(clock_1_out));
  not not_1 (not_1_out, CLK_RUN);
  Button CLK_STEP (.out(CLK_STEP_out));
  Button u_RST (.out(RST));
  assign out_45 = in_5 ? in_3 : 8'bz;  // Controlled_Buffer controlled_buffer_5
  assign out_45 = Z_TO_DATA ? out_51 : 8'bz;  // Controlled_Buffer controlled_buffer_6
  and and_1 (and_1_out, clock_1_out, CLK_RUN);
  and and_2 (and_2_out, not_1_out, CLK_STEP_out);
  not not_2 (not_2_out, CLK_HLT);
  assign out_45 = IP_LO_TO_DATA ? out_47[7:0] : 8'bz;  // Controlled_Buffer controlled_buffer_7
  assign controlled_buffer_8_out = DATA_TO_IP_LO ? out_45 : 8'bz;  // Controlled_Buffer controlled_buffer_8
  assign controlled_buffer_9_out = DATA_TO_MAR_LO ? out_45 : 8'bz;  // Controlled_Buffer controlled_buffer_9
  assign out_52 = DATA_TO_MDR ? out_45 : 8'bz;  // Controlled_Buffer controlled_buffer_10
  assign out_45 = MDR_TO_DATA ? out_52 : 8'bz;  // Controlled_Buffer controlled_buffer_11
  assign out_45 = L_TO_DATA ? out_55 : 8'bz;  // Controlled_Buffer controlled_buffer_12
  assign controlled_buffer_13_out = DATA_TO_L ? out_45 : 8'bz;  // Controlled_Buffer controlled_buffer_13
  assign out_45 = TL_TO_DATA ? out_60 : 8'bz;  // Controlled_Buffer controlled_buffer_14
  not not_3 (not_3_out, DATA_TO_TL);
  assign controlled_buffer_15_out = DATA_TO_TL ? out_45 : 8'bz;  // Controlled_Buffer controlled_buffer_15
  or or_1 (or_1_out, and_1_out, and_2_out);
  and and_3 (CLK, or_1_out, not_2_out);
  assign out_45 = IP_HI_TO_DATA ? out_47[15:8] : 8'bz;  // Controlled_Buffer controlled_buffer_16
  nor nor_2 (nor_2_out, DATA_TO_IP_LO, ADDR_TO_IP);
  assign controlled_buffer_8_out = nor_2_out ? out_47[7:0] : 8'bz;  // Controlled_Buffer controlled_buffer_17
  assign controlled_buffer_18_out = DATA_TO_IP_HI ? out_45 : 8'bz;  // Controlled_Buffer controlled_buffer_18
  nor nor_3 (nor_3_out, DATA_TO_MAR_LO, ADDR_TO_MAR);
  assign controlled_buffer_9_out = nor_3_out ? out_50[7:0] : 8'bz;  // Controlled_Buffer controlled_buffer_19
  assign controlled_buffer_20_out = DATA_TO_MAR_HI ? out_45 : 8'bz;  // Controlled_Buffer controlled_buffer_20
  not not_4 (not_4_out, DATA_TO_MDR);
  assign out_45 = H_TO_DATA ? out_54 : 8'bz;  // Controlled_Buffer controlled_buffer_21
  nor nor_4 (nor_4_out, DATA_TO_L, ADDR_TO_HL);
  assign controlled_buffer_13_out = nor_4_out ? out_55 : 8'bz;  // Controlled_Buffer controlled_buffer_22
  assign controlled_buffer_23_out = DATA_TO_H ? out_45 : 8'bz;  // Controlled_Buffer controlled_buffer_23
  assign out_45 = TH_TO_DATA ? out_59 : 8'bz;  // Controlled_Buffer controlled_buffer_24
  not not_5 (not_5_out, DATA_TO_TH);
  assign controlled_buffer_15_out = not_3_out ? out_60 : 8'bz;  // Controlled_Buffer controlled_buffer_25
  assign controlled_buffer_26_out = not_5_out ? out_59 : 8'bz;  // Controlled_Buffer controlled_buffer_26
  assign controlled_buffer_26_out = DATA_TO_TH ? out_45 : 8'bz;  // Controlled_Buffer controlled_buffer_27
  or or_2 (or_2_out, DATA_TO_TH, DATA_TO_TL);
  not not_6 (minus_CLK, CLK);
  nor nor_5 (nor_5_out, DATA_TO_IP_HI, ADDR_TO_IP);
  assign controlled_buffer_18_out = nor_5_out ? out_47[15:8] : 8'bz;  // Controlled_Buffer controlled_buffer_28
  or or_3 (or_3_out, DATA_TO_IP_HI, DATA_TO_IP_LO, ADDR_TO_IP);
  nor nor_6 (nor_6_out, DATA_TO_MAR_HI, ADDR_TO_MAR);
  assign controlled_buffer_20_out = nor_6_out ? out_50[15:8] : 8'bz;  // Controlled_Buffer controlled_buffer_29
  or or_4 (or_4_out, DATA_TO_MAR_HI, DATA_TO_MAR_LO, ADDR_TO_MAR);
  nor nor_7 (nor_7_out, DATA_TO_H, ADDR_TO_HL);
  assign controlled_buffer_23_out = nor_7_out ? out_54 : 8'bz;  // Controlled_Buffer controlled_buffer_30
  or or_5 (or_5_out, DATA_TO_H, DATA_TO_L, ADDR_TO_HL);
  Counter #(.width(16), .max('hffff)) counter_1 (
    .load(or_3_out), .D({controlled_buffer_18_out, controlled_buffer_8_out}), .count(IP_INC), .Q(out_47),
    .clk(CLK), .clr(RST));  // open: carry
  Counter #(.width(16), .max('hffff)) counter_2 (
    .load(or_4_out), .D({controlled_buffer_20_out, controlled_buffer_9_out}), .count(MAR_INC), .Q(out_50),
    .clk(CLK));  // open: carry, clr
  Register #(.width(16)) register_8 (
    .D({controlled_buffer_23_out, controlled_buffer_13_out}), .en(or_5_out), .Q({out_54, out_55}), .clk(CLK),
    .clr(RST));
  Register #(.width(16)) register_9 (
    .D({controlled_buffer_26_out, controlled_buffer_15_out}), .en(or_2_out), .Q({out_59, out_60}), .clk(CLK),
    .clr(RST));
  RAM #(.addrWidth(16)) ram_1 (.addr(out_50), .data(out_52), .sel(1'b1), .clk(CLK), .ld(not_4_out));  // open: clr
  assign out_46 = in_6 ? in_4 : 16'bz;  // Controlled_Buffer controlled_buffer_31
  assign out_46 = IP_TO_ADDR ? out_47 : 16'bz;  // Controlled_Buffer controlled_buffer_32
  assign {controlled_buffer_18_out, controlled_buffer_8_out} = ADDR_TO_IP ? out_46 : 16'bz;  // Controlled_Buffer controlled_buffer_33
  assign {controlled_buffer_20_out, controlled_buffer_9_out} = ADDR_TO_MAR ? out_46 : 16'bz;  // Controlled_Buffer controlled_buffer_34
  assign out_46 = HL_TO_ADDR ? {out_54, out_55} : 16'bz;  // Controlled_Buffer controlled_buffer_35
  assign {controlled_buffer_23_out, controlled_buffer_13_out} = ADDR_TO_HL ? out_46 : 16'bz;  // Controlled_Buffer controlled_buffer_36
  assign out_46 = T_TO_ADDR ? {out_59, out_60} : 16'bz;  // Controlled_Buffer controlled_buffer_37

  assign out_56 = {out_54, out_55};
  assign out_61 = {out_59, out_60};

  // Notes on the sheet:
  //   Adder / Substractor
  //   Flags
  //   A Register
  //   X Register
  //   Y Register
  //   B Register
  //   C Register
  //   D Register
  //   Z Register
  //   8-Bit Data Bus
  //   Clock
  //   TH Register
  //   TL Register
  //   T Register
  //   Instruction Pointer
  //   Memory Address Register
  //   Memory Data Register
  //   H Register
  //   L Register
  //   HL Register
  //   16-Bit Address Bus
endmodule
